// Logisim project ALU.circ as structural Verilog: 19 circuits, main circuit main
module main (
  input  a,
  input  in_2,
  input  in_3,
  input  in_4,
  input  b,
  input  in_6,
  input  in_7,
  input  in_8,
  input  s0,
  input  s1,
  input  M
);

  wire alu_1_out_12, alu_1_out_13, alu_1_out_14, alu_1_out_15, alu_1_out_16, alu_1_out_17, alu_1_out_18,
       alu_1_out_19, n7_segment_decoder_1_out_6, n7_segment_decoder_1_out_7, n7_segment_decoder_1_out_8,
       n7_segment_decoder_1_out_9, n7_segment_decoder_1_out_10, n7_segment_decoder_1_out_11,
       n7_segment_decoder_1_out_12;

  ALU alu_1 (
    .a0___a3(a), .in_2(in_2), .in_3(in_3), .in_4(in_4), .b0___b3(b), .in_6(in_6), .in_7(in_7), .in_8(in_8),
    .s0(s0), .s1(s1), .M(M), .out_17(alu_1_out_17), .out_18(alu_1_out_18), .out_19(alu_1_out_19),
    .out_12(alu_1_out_12), .out_13(alu_1_out_13), .out_14(alu_1_out_14), .out_15(alu_1_out_15),
    .out_16(alu_1_out_16));
  LED led_1 (.in(alu_1_out_16));
  LED led_2 (.in(alu_1_out_17));
  LED led_3 (.in(alu_1_out_18));
  LED led_4 (.in(alu_1_out_19));
  _7_Segment_Decoder u_7_segment_decoder_1 (
    .d(alu_1_out_12), .c(alu_1_out_13), .b(alu_1_out_14), .a(alu_1_out_15),
    .out_6(n7_segment_decoder_1_out_6), .out_7(n7_segment_decoder_1_out_7),
    .out_8(n7_segment_decoder_1_out_8), .out_9(n7_segment_decoder_1_out_9),
    .out_10(n7_segment_decoder_1_out_10), .out_11(n7_segment_decoder_1_out_11),
    .out_12(n7_segment_decoder_1_out_12), .M(M));
  _7_Segment_Display u_7_segment_display_1 (
    .g(n7_segment_decoder_1_out_12), .f(n7_segment_decoder_1_out_11), .a(n7_segment_decoder_1_out_6),
    .b(n7_segment_decoder_1_out_7), .e(n7_segment_decoder_1_out_10), .d(n7_segment_decoder_1_out_9),
    .c(n7_segment_decoder_1_out_8));  // open: dp
endmodule

module Adder (
  input  a0,
  input  b0,
  input  a1,
  input  b1,
  input  a2,
  input  b2,
  input  a3,
  input  b3,
  output out_9,
  output out_10,
  output out_11,
  output out_12,
  output out_13
);

  wire full_adder_1_carry_out, full_adder_2_carry_out, half_adder_1_carry_out;

  Half_Adder half_adder_1 (.A0(a0), .B0(b0), .out_3(out_9), .Carry_Out(half_adder_1_carry_out));
  Full_Adder full_adder_1 (
    .x(a1), .y(b1), .cin(half_adder_1_carry_out), .Sum(out_10), .Carry_Out(full_adder_1_carry_out));
  Full_Adder full_adder_2 (
    .x(a2), .y(b2), .cin(full_adder_1_carry_out), .Sum(out_11), .Carry_Out(full_adder_2_carry_out));
  Full_Adder full_adder_3 (.x(a3), .y(b3), .cin(full_adder_2_carry_out), .Sum(out_12), .Carry_Out(out_13));

  // Notes on the sheet:
  //   Half Adder
  //   Full Adders
endmodule

module Half_Adder (
  input  A0,
  input  B0,
  output out_3,
  output Carry_Out
);

  xor xor_1 (out_3, A0, B0);
  and and_1 (Carry_Out, A0, B0);

  // Notes on the sheet:
  //   Half Adder
  //   Sum
endmodule

module Full_Adder (
  input  x,
  input  y,
  input  cin,
  output Sum,
  output Carry_Out
);

  wire half_adder_1_carry_out, half_adder_1_out_3, half_adder_2_carry_out;

  Half_Adder half_adder_1 (.A0(x), .B0(y), .out_3(half_adder_1_out_3), .Carry_Out(half_adder_1_carry_out));
  Half_Adder half_adder_2 (.A0(half_adder_1_out_3), .B0(cin), .out_3(Sum), .Carry_Out(half_adder_2_carry_out));
  or or_1 (Carry_Out, half_adder_2_carry_out, half_adder_1_carry_out);
endmodule

module Arithmetic_Unit (
  input  a0___a3,
  input  in_2,
  input  in_3,
  input  in_4,
  input  b0___b3,
  input  in_6,
  input  in_7,
  input  in_8,
  input  s0,
  input  s1,
  output out_11,
  output out_12,
  output out_13,
  output out_14,
  output out_15,
  output out_16
);

  wire adder_1_out_9, adder_1_out_10, adder_1_out_11, adder_1_out_12, incrementer_1_out_5,
       incrementer_1_out_6, incrementer_1_out_7, incrementer_1_out_8, n2_s_comp_negator_1_out_5,
       n2_s_comp_negator_1_out_6, n2_s_comp_negator_1_out_7, n2_s_comp_negator_1_out_8, subtractor_1_out_9,
       subtractor_1_out_11, subtractor_1_out_12, subtractor_1_s0___s3;

  Adder adder_1 (
    .a0(a0___a3), .b0(b0___b3), .a1(in_2), .b1(in_6), .a2(in_3), .b2(in_7), .a3(in_4), .b3(in_8),
    .out_9(adder_1_out_9), .out_10(adder_1_out_10), .out_11(adder_1_out_11), .out_12(adder_1_out_12));  // open: out_13
  Subtractor subtractor_1 (
    .in_1(a0___a3), .in_2(in_2), .a0___a3(in_3), .in_4(in_4), .in_5(b0___b3), .in_6(in_6), .b0___b3(in_7),
    .in_8(in_8), .out_9(subtractor_1_out_9), .s0___s3(subtractor_1_s0___s3), .out_11(subtractor_1_out_11),
    .out_12(subtractor_1_out_12));  // open: cout
  _2_s_Comp_Negator u_2_s_comp_negator_1 (
    .in_1(b0___b3), .in_2(in_6), .b0___b3(in_7), .in_4(in_8), .out_5(n2_s_comp_negator_1_out_5),
    .out_6(n2_s_comp_negator_1_out_6), .out_7(n2_s_comp_negator_1_out_7), .out_8(n2_s_comp_negator_1_out_8),
    .out_9(out_15));
  Incrementer incrementer_1 (
    .in_1(a0___a3), .in_2(in_2), .in_3(in_3), .in_4(in_4), .out_9(out_16), .out_5(incrementer_1_out_5),
    .out_6(incrementer_1_out_6), .out_7(incrementer_1_out_7), .out_8(incrementer_1_out_8));
  _4_Channel_4_bit_Multiplexer u_4_channel_4_bit_multiplexer_1 (
    .in_1(adder_1_out_9), .in_2(adder_1_out_10), .in_3(adder_1_out_11), .in_4(adder_1_out_12),
    .in_5(subtractor_1_out_9), .in_6(subtractor_1_s0___s3), .in_7(subtractor_1_out_11),
    .in_8(subtractor_1_out_12), .in_9(n2_s_comp_negator_1_out_5), .in_10(n2_s_comp_negator_1_out_6),
    .in_11(n2_s_comp_negator_1_out_7), .in_12(n2_s_comp_negator_1_out_8), .in_13(incrementer_1_out_5),
    .in_14(incrementer_1_out_6), .in_15(incrementer_1_out_7), .in_16(incrementer_1_out_8), .s0(s0), .s1(s1),
    .out_19(out_11), .out_20(out_12), .out_21(out_13), .out_22(out_14));
endmodule

module Subtractor (
  input  in_1,
  input  in_2,
  input  a0___a3,
  input  in_4,
  input  in_5,
  input  in_6,
  input  b0___b3,
  input  in_8,
  output out_9,
  output s0___s3,
  output out_11,
  output out_12,
  output cout
);

  wire not_1_out, not_2_out, not_3_out, not_4_out;

  not not_1 (not_1_out, in_5);
  not not_2 (not_2_out, in_6);
  not not_3 (not_3_out, b0___b3);
  not not_4 (not_4_out, in_8);
  Adder__With_Cin adder_with_cin_1 (
    .cin(1'b1), .a0(in_1), .b0(not_1_out), .a1(in_2), .b1(not_2_out), .a2(a0___a3), .b2(not_3_out),
    .a3(in_4), .b3(not_4_out), .s0(out_9), .s1(s0___s3), .s2(out_11), .s3(out_12), .cout(cout));
endmodule

module Adder__With_Cin (
  input  cin,
  input  a0,
  input  b0,
  input  a1,
  input  b1,
  input  a2,
  input  b2,
  input  a3,
  input  b3,
  output s0,
  output s1,
  output s2,
  output s3,
  output cout
);

  wire full_adder_1_carry_out, full_adder_2_carry_out, full_adder_3_carry_out;

  Full_Adder full_adder_1 (.x(a0), .y(b0), .cin(cin), .Sum(s0), .Carry_Out(full_adder_1_carry_out));
  Full_Adder full_adder_2 (.x(a1), .y(b1), .cin(full_adder_1_carry_out), .Sum(s1), .Carry_Out(full_adder_2_carry_out));
  Full_Adder full_adder_3 (.x(a2), .y(b2), .cin(full_adder_2_carry_out), .Sum(s2), .Carry_Out(full_adder_3_carry_out));
  Full_Adder full_adder_4 (.x(a3), .y(b3), .cin(full_adder_3_carry_out), .Sum(s3), .Carry_Out(cout));
endmodule

module _2_s_Comp_Negator (
  input  in_1,
  input  in_2,
  input  b0___b3,
  input  in_4,
  output out_5,
  output out_6,
  output out_7,
  output out_8,
  output out_9
);

  wire not_1_out, not_2_out, not_3_out, not_4_out;

  not not_1 (not_1_out, in_1);
  not not_2 (not_2_out, in_2);
  not not_3 (not_3_out, b0___b3);
  not not_4 (not_4_out, in_4);
  Adder adder_1 (
    .a0(1'b1), .b0(not_1_out), .a1(1'b0), .b1(not_2_out), .a2(1'b0), .b2(not_3_out), .a3(1'b0),
    .b3(not_4_out), .out_9(out_5), .out_10(out_6), .out_11(out_7), .out_12(out_8), .out_13(out_9));
endmodule

module Incrementer (
  input  in_1,
  input  in_2,
  input  in_3,
  input  in_4,
  output out_5,
  output out_6,
  output out_7,
  output out_8,
  output out_9
);

  Adder adder_1 (
    .a0(in_1), .b0(1'b1), .a1(in_2), .b1(1'b0), .a2(in_3), .b2(1'b0), .a3(in_4), .b3(1'b0), .out_9(out_5),
    .out_10(out_6), .out_11(out_7), .out_12(out_8), .out_13(out_9));
endmodule

module _4_Channel_4_bit_Multiplexer (
  input  in_1,
  input  in_2,
  input  in_3,
  input  in_4,
  input  in_5,
  input  in_6,
  input  in_7,
  input  in_8,
  input  in_9,
  input  in_10,
  input  in_11,
  input  in_12,
  input  in_13,
  input  in_14,
  input  in_15,
  input  in_16,
  input  s0,
  input  s1,
  output out_19,
  output out_20,
  output out_21,
  output out_22
);

  wire and_1_out, and_2_out, and_3_out, and_4_out, and_5_out, and_6_out, and_7_out, and_8_out, and_9_out,
       and_10_out, and_11_out, and_12_out, and_13_out, and_14_out, and_15_out, and_16_out, not_1_out,
       not_2_out, not_3_out, not_4_out, not_5_out, not_6_out, not_7_out, not_8_out, not_9_out, not_10_out,
       not_11_out, not_12_out, not_13_out, not_14_out, not_15_out, not_16_out;

  not not_1 (not_1_out, s0);
  not not_2 (not_2_out, s1);
  not not_3 (not_3_out, s0);
  not not_4 (not_4_out, s1);
  not not_5 (not_5_out, s0);
  not not_6 (not_6_out, s1);
  not not_7 (not_7_out, s0);
  not not_8 (not_8_out, s1);
  not not_9 (not_9_out, s0);
  not not_10 (not_10_out, s0);
  not not_11 (not_11_out, s0);
  not not_12 (not_12_out, s0);
  not not_13 (not_13_out, s1);
  not not_14 (not_14_out, s1);
  not not_15 (not_15_out, s1);
  not not_16 (not_16_out, s1);
  and and_1 (and_1_out, in_1, not_1_out, not_2_out);
  and and_2 (and_2_out, in_2, not_3_out, not_4_out);
  and and_3 (and_3_out, in_3, not_5_out, not_6_out);
  and and_4 (and_4_out, in_4, not_7_out, not_8_out);
  and and_5 (and_5_out, in_5, not_9_out, s1);
  and and_6 (and_6_out, in_6, not_10_out, s1);
  and and_7 (and_7_out, in_7, not_11_out, s1);
  and and_8 (and_8_out, in_8, not_12_out, s1);
  and and_9 (and_9_out, in_9, s0, not_13_out);
  and and_10 (and_10_out, in_10, s0, not_14_out);
  and and_11 (and_11_out, in_11, s0, not_15_out);
  and and_12 (and_12_out, in_12, s0, not_16_out);
  and and_13 (and_13_out, in_13, s0, s1);
  and and_14 (and_14_out, in_14, s0, s1);
  and and_15 (and_15_out, in_15, s0, s1);
  and and_16 (and_16_out, in_16, s0, s1);
  or or_1 (out_19, and_1_out, and_5_out, and_9_out, and_13_out);
  or or_2 (out_20, and_2_out, and_6_out, and_10_out, and_14_out);
  or or_3 (out_21, and_3_out, and_7_out, and_11_out, and_15_out);
  or or_4 (out_22, and_4_out, and_8_out, and_12_out, and_16_out);
endmodule

module AND (
  input  in_1,
  input  in_2,
  input  in_3,
  input  in_4,
  input  in_5,
  input  in_6,
  input  in_7,
  input  in_8,
  output out_9,
  output out_10,
  output out_11,
  output out_12
);

  and and_1 (out_9, in_1, in_5);
  and and_2 (out_10, in_2, in_6);
  and and_3 (out_11, in_3, in_7);
  and and_4 (out_12, in_4, in_8);
endmodule

module OR (
  input  in_1,
  input  in_2,
  input  in_3,
  input  in_4,
  input  in_5,
  input  in_6,
  input  in_7,
  input  in_8,
  output out_9,
  output out_10,
  output out_11,
  output out_12
);

  or or_1 (out_9, in_1, in_5);
  or or_2 (out_10, in_2, in_6);
  or or_3 (out_11, in_3, in_7);
  or or_4 (out_12, in_4, in_8);
endmodule

module XOR (
  input  in_1,
  input  in_2,
  input  in_3,
  input  in_4,
  input  in_5,
  input  in_6,
  input  in_7,
  input  in_8,
  output out_9,
  output out_10,
  output out_11,
  output out_12
);

  xor xor_1 (out_9, in_1, in_5);
  xor xor_2 (out_10, in_2, in_6);
  xor xor_3 (out_11, in_3, in_7);
  xor xor_4 (out_12, in_4, in_8);
endmodule

module _1_s_Comp (
  input  in_1,
  input  in_2,
  input  in_3,
  input  in_4,
  output out_5,
  output out_6,
  output out_7,
  output out_8
);

  not not_1 (out_5, in_1);
  not not_2 (out_6, in_2);
  not not_3 (out_7, in_3);
  not not_4 (out_8, in_4);
endmodule

module Logic_Unit (
  input  a0___a3,
  input  in_2,
  input  in_3,
  input  in_4,
  input  b0___b3,
  input  in_6,
  input  in_7,
  input  in_8,
  input  s0,
  input  s1,
  output out_11,
  output out_12,
  output out_13,
  output out_14
);

  wire and_1_out_9, and_1_out_10, and_1_out_11, and_1_out_12, n1_s_comp_1_out_5, n1_s_comp_1_out_6,
       n1_s_comp_1_out_7, n1_s_comp_1_out_8, or_1_out_9, or_1_out_10, or_1_out_11, or_1_out_12, xor_1_out_9,
       xor_1_out_10, xor_1_out_11, xor_1_out_12;

  AND and_1 (
    .in_1(a0___a3), .in_2(in_2), .in_3(in_3), .in_4(in_4), .in_5(b0___b3), .in_6(in_6), .in_7(in_7),
    .in_8(in_8), .out_9(and_1_out_9), .out_10(and_1_out_10), .out_11(and_1_out_11), .out_12(and_1_out_12));
  OR or_1 (
    .in_1(a0___a3), .in_2(in_2), .in_3(in_3), .in_4(in_4), .in_5(b0___b3), .in_6(in_6), .in_7(in_7),
    .in_8(in_8), .out_9(or_1_out_9), .out_10(or_1_out_10), .out_11(or_1_out_11), .out_12(or_1_out_12));
  XOR xor_1 (
    .in_1(a0___a3), .in_2(in_2), .in_3(in_3), .in_4(in_4), .in_5(b0___b3), .in_6(in_6), .in_7(in_7),
    .in_8(in_8), .out_9(xor_1_out_9), .out_10(xor_1_out_10), .out_11(xor_1_out_11), .out_12(xor_1_out_12));
  _1_s_Comp u_1_s_comp_1 (
    .in_1(a0___a3), .in_2(in_2), .in_3(in_3), .in_4(in_4), .out_5(n1_s_comp_1_out_5),
    .out_6(n1_s_comp_1_out_6), .out_7(n1_s_comp_1_out_7), .out_8(n1_s_comp_1_out_8));
  _4_Channel_4_bit_Multiplexer u_4_channel_4_bit_multiplexer_1 (
    .in_1(and_1_out_9), .in_2(and_1_out_10), .in_3(and_1_out_11), .in_4(and_1_out_12), .in_5(or_1_out_9),
    .in_6(or_1_out_10), .in_7(or_1_out_11), .in_8(or_1_out_12), .in_9(xor_1_out_9), .in_10(xor_1_out_10),
    .in_11(xor_1_out_11), .in_12(xor_1_out_12), .in_13(n1_s_comp_1_out_5), .in_14(n1_s_comp_1_out_6),
    .in_15(n1_s_comp_1_out_7), .in_16(n1_s_comp_1_out_8), .s0(s0), .s1(s1), .out_19(out_11), .out_20(out_12),
    .out_21(out_13), .out_22(out_14));
endmodule

module Comparator (
  input  in_1,
  input  in_2,
  input  in_3,
  input  in_4,
  input  in_5,
  input  in_6,
  input  in_7,
  input  in_8,
  output Equals,
  output A_Less_Than_B,
  output out_11
);

  wire and_1_out, and_2_out, and_3_out, and_4_out, not_1_out, not_2_out, not_3_out, not_4_out, xnor_1_out,
       xnor_2_out, xnor_3_out, xor_1_out_9, xor_1_out_10, xor_1_out_11, xor_1_out_12;

  xnor xnor_1 (xnor_1_out, in_4, in_8);
  not xnor_2 (xnor_2_out, in_7);  // XNOR_Gate
  not xnor_3 (xnor_3_out, in_6);  // XNOR_Gate
  XOR xor_1 (
    .in_1(in_1), .in_2(in_2), .in_3(in_3), .in_4(in_4), .in_5(in_5), .in_6(in_6), .in_7(in_7), .in_8(in_8),
    .out_9(xor_1_out_9), .out_10(xor_1_out_10), .out_11(xor_1_out_11), .out_12(xor_1_out_12));
  not not_1 (not_1_out, xor_1_out_9);
  not not_2 (not_2_out, xor_1_out_10);
  not not_3 (not_3_out, xor_1_out_11);
  not not_4 (not_4_out, xor_1_out_12);
  and and_1 (and_1_out, in_4, ~in_8);  // AND_Gate
  and and_2 (and_2_out, xnor_1_out, in_3, ~in_7);  // AND_Gate
  and and_3 (and_3_out, in_2, xnor_1_out, xnor_2_out, ~in_6);  // AND_Gate
  and and_4 (and_4_out, in_1, xnor_1_out, xnor_2_out, xnor_3_out, ~in_5);  // AND_Gate
  and and_5 (Equals, not_1_out, not_2_out, not_3_out, not_4_out);
  or or_1 (out_11, and_1_out, and_2_out, and_3_out, and_4_out);
  nor nor_1 (A_Less_Than_B, Equals, out_11);

  // Notes on the sheet:
  //   A Greater Than B
endmodule

module ALU (
  input  a0___a3,
  input  in_2,
  input  in_3,
  input  in_4,
  input  b0___b3,
  input  in_6,
  input  in_7,
  input  in_8,
  input  s0,
  input  s1,
  input  M,
  output out_12,
  output out_13,
  output out_14,
  output out_15,
  output out_16,
  output out_17,
  output out_18,
  output out_19
);

  wire and_1_out, and_2_out, arithmetic_unit_1_out_11, arithmetic_unit_1_out_12, arithmetic_unit_1_out_13,
       arithmetic_unit_1_out_14, arithmetic_unit_1_out_15, arithmetic_unit_1_out_16,
       comparator_1_a_less_than_b, comparator_1_equals, comparator_1_out_11, logic_unit_1_out_11,
       logic_unit_1_out_12, logic_unit_1_out_13, logic_unit_1_out_14;

  Comparator comparator_1 (
    .Equals(comparator_1_equals), .A_Less_Than_B(comparator_1_a_less_than_b), .out_11(comparator_1_out_11),
    .in_1(a0___a3), .in_2(in_2), .in_3(in_3), .in_4(in_4), .in_5(b0___b3), .in_6(in_6), .in_7(in_7),
    .in_8(in_8));
  Arithmetic_Unit arithmetic_unit_1 (
    .a0___a3(a0___a3), .in_2(in_2), .in_3(in_3), .in_4(in_4), .b0___b3(b0___b3), .in_6(in_6), .in_7(in_7),
    .in_8(in_8), .s0(s0), .s1(s1), .out_11(arithmetic_unit_1_out_11), .out_12(arithmetic_unit_1_out_12),
    .out_13(arithmetic_unit_1_out_13), .out_14(arithmetic_unit_1_out_14), .out_15(arithmetic_unit_1_out_15),
    .out_16(arithmetic_unit_1_out_16));
  Logic_Unit logic_unit_1 (
    .a0___a3(a0___a3), .in_2(in_2), .in_3(in_3), .in_4(in_4), .b0___b3(b0___b3), .in_6(in_6), .in_7(in_7),
    .in_8(in_8), .s0(s0), .s1(s1), .out_11(logic_unit_1_out_11), .out_12(logic_unit_1_out_12),
    .out_13(logic_unit_1_out_13), .out_14(logic_unit_1_out_14));
  _2_Channel_4_Bit_Multiplexer u_2_channel_4_bit_multiplexer_1 (
    .in_1(arithmetic_unit_1_out_11), .in_2(arithmetic_unit_1_out_12), .in_3(arithmetic_unit_1_out_13),
    .in_4(arithmetic_unit_1_out_14), .in_5(logic_unit_1_out_11), .in_6(logic_unit_1_out_12),
    .in_7(logic_unit_1_out_13), .in_8(logic_unit_1_out_14), .in_9(M), .out_10(out_12), .out_11(out_13),
    .out_12(out_14), .out_13(out_15));
  and and_1 (and_1_out, ~M, arithmetic_unit_1_out_15, s0, ~s1);  // AND_Gate
  and and_2 (and_2_out, ~M, arithmetic_unit_1_out_16, s1, s0);  // AND_Gate
  and and_3 (out_17, ~M, comparator_1_equals);  // AND_Gate
  and and_4 (out_18, ~M, comparator_1_a_less_than_b);  // AND_Gate
  and and_5 (out_19, ~M, comparator_1_out_11);  // AND_Gate
  or or_1 (out_16, and_1_out, and_2_out);
endmodule

module _2_Channel_4_Bit_Multiplexer (
  input  in_1,
  input  in_2,
  input  in_3,
  input  in_4,
  input  in_5,
  input  in_6,
  input  in_7,
  input  in_8,
  input  in_9,
  output out_10,
  output out_11,
  output out_12,
  output out_13
);

  wire and_1_out, and_2_out, and_3_out, and_4_out, and_5_out, and_6_out, and_7_out, and_8_out, not_1_out;

  not not_1 (not_1_out, in_9);
  and and_1 (and_1_out, in_1, in_9);
  and and_2 (and_2_out, in_2, in_9);
  and and_3 (and_3_out, in_3, in_9);
  and and_4 (and_4_out, in_4, in_9);
  and and_5 (and_5_out, in_5, not_1_out);
  and and_6 (and_6_out, in_6, not_1_out);
  and and_7 (and_7_out, in_7, not_1_out);
  and and_8 (and_8_out, in_8, not_1_out);
  or or_1 (out_10, and_1_out, and_5_out);
  or or_2 (out_11, and_2_out, and_6_out);
  or or_3 (out_12, and_3_out, and_7_out);
  or or_4 (out_13, and_4_out, and_8_out);
endmodule

module _7_Segment_Decoder (
  input  M,
  input  d,
  input  c,
  input  b,
  input  a,
  output out_6,
  output out_7,
  output out_8,
  output out_9,
  output out_10,
  output out_11,
  output out_12
);

  wire and_1_out, and_2_out, and_3_out, and_4_out, and_5_out, and_6_out, and_7_out, and_8_out, and_9_out,
       and_10_out, and_11_out, and_12_out, and_13_out, and_14_out, and_15_out, and_16_out, and_17_out,
       and_18_out, and_19_out, and_20_out, and_21_out, and_22_out, and_23_out, and_24_out, and_25_out,
       and_26_out, and_27_out, and_28_out, and_29_out, and_30_out, and_31_out, and_32_out, and_33_out,
       and_34_out, and_35_out, or_1_out, or_2_out, or_3_out, or_4_out, or_5_out, or_6_out, or_7_out;

  and and_1 (and_1_out, ~a, c);  // AND_Gate
  and and_2 (and_2_out, a, ~d);  // AND_Gate
  and and_3 (and_3_out, b, c);
  and and_4 (and_4_out, ~b, ~d);  // AND_Gate
  and and_5 (and_5_out, a, ~b, ~c);  // AND_Gate
  and and_6 (and_6_out, ~a, b, d);  // AND_Gate
  and and_7 (and_7_out, ~a, ~b);  // AND_Gate
  and and_8 (and_8_out, ~b, ~d);  // AND_Gate
  and and_9 (and_9_out, ~a, ~c, ~d);  // AND_Gate
  and and_10 (and_10_out, ~a, c, d);  // AND_Gate
  and and_11 (and_11_out, a, ~c, d);  // AND_Gate
  and and_12 (and_12_out, a, ~b);  // AND_Gate
  and and_13 (and_13_out, ~a, b);  // AND_Gate
  and and_14 (and_14_out, ~a, ~c);  // AND_Gate
  and and_15 (and_15_out, ~a, d);  // AND_Gate
  and and_16 (and_16_out, ~c, d);  // AND_Gate
  and and_17 (and_17_out, a, ~c);  // AND_Gate
  and and_18 (and_18_out, ~a, ~b, ~d);  // AND_Gate
  and and_19 (and_19_out, ~b, c, d);  // AND_Gate
  and and_20 (and_20_out, b, c, ~d);  // AND_Gate
  and and_21 (and_21_out, b, ~c, d);  // AND_Gate
  and and_22 (and_22_out, a, b);
  and and_23 (and_23_out, a, c);
  and and_24 (and_24_out, ~b, ~d);  // AND_Gate
  and and_25 (and_25_out, c, ~d);  // AND_Gate
  and and_26 (and_26_out, a, ~b);  // AND_Gate
  and and_27 (and_27_out, a, c);
  and and_28 (and_28_out, b, ~d);  // AND_Gate
  and and_29 (and_29_out, ~c, ~d);  // AND_Gate
  and and_30 (and_30_out, ~a, b, ~c);  // AND_Gate
  and and_31 (and_31_out, a, ~b);  // AND_Gate
  and and_32 (and_32_out, a, d);
  and and_33 (and_33_out, ~b, c);  // AND_Gate
  and and_34 (and_34_out, c, ~d);  // AND_Gate
  and and_35 (and_35_out, ~a, b, ~c);  // AND_Gate
  or or_1 (or_1_out, and_1_out, and_2_out, and_3_out, and_4_out, and_5_out, and_6_out);
  or or_2 (or_2_out, and_7_out, and_8_out, and_9_out, and_10_out, and_11_out);
  or or_3 (or_3_out, and_12_out, and_13_out, and_14_out, and_15_out, and_16_out);
  or or_4 (or_4_out, and_17_out, and_18_out, and_19_out, and_20_out, and_21_out);
  or or_5 (or_5_out, and_22_out, and_23_out, and_24_out, and_25_out);
  or or_6 (or_6_out, and_26_out, and_27_out, and_28_out, and_29_out, and_30_out);
  or or_7 (or_7_out, and_31_out, and_32_out, and_33_out, and_34_out, and_35_out);
  and and_36 (out_6, M, or_1_out);
  and and_37 (out_7, M, or_2_out);
  and and_38 (out_8, M, or_3_out);
  and and_39 (out_9, M, or_4_out);
  and and_40 (out_10, M, or_5_out);
  and and_41 (out_11, M, or_6_out);
  and and_42 (out_12, M, or_7_out);

  // Notes on the sheet:
  //   a
  //   b
  //   c
  //   d
  //   e
  //   f
  //   g
endmodule
